# Fritzing sketch Current sensor (saved by Fritzing 0.9.10b)
breadboards: 1

parts:
  Raspberry_Pi1 = Raspberry Pi 2
  TRS1 = Audio Jack (TRS) 3.5mm [package="PG203J [THT]"]
  C3 = Electrolytic Capacitor [capacitance=10µF voltage=50V package="100 mil [THT, electrolytic]"]
  R1 = Resistor [tolerance=±5% power=0.5W resistance=100k package=THT]
  R2 = Resistor [tolerance=±5% power=0.5W resistance=100k package=THT]
  ADC1 = MCP3008 [package=dil16]
  TRS2 = Audio Jack (TRS) 3.5mm [package="PG203J [THT]"]
  C4 = Electrolytic Capacitor [capacitance=10µF voltage=50V package="100 mil [THT, electrolytic]"]
  R3 = Resistor [tolerance=±5% power=0.5W resistance=100k package=THT]
  R4 = Resistor [tolerance=±5% power=0.5W resistance=100k package=THT]
  U1 = Transformer [package=transformer]
  U2 = Transformer [package=transformer]

nets:
  3V3: Raspberry_Pi1.3v3, Raspberry_Pi1.3V3, R2.Pin_0, ADC1.VDD, R4.Pin_0
  N1: Raspberry_Pi1.GPIO10, ADC1.Din
  N2: Raspberry_Pi1.GPIO9, ADC1.Dout
  N3: Raspberry_Pi1.GPIO11, ADC1.CLK
  N4: Raspberry_Pi1.GND, C3.-, R1.Pin_0, ADC1.AGND, C4.-, R3.Pin_0
  N5: Raspberry_Pi1.GPIO8, ADC1.CS/SHDN
  N6: TRS1.Sleeve, C3.+, R1.Pin_1, R2.Pin_1, U1.4
  N7: TRS1.Tip, ADC1.CH0, U1.1
  N8: ADC1.CH1, TRS2.Tip, U2.1
  N9: TRS2.Sleeve, C4.+, R3.Pin_1, R4.Pin_1, U2.4
